# Fritzing sketch Wiring (saved by Fritzing 0.9.3b)

parts:
  part = ESP8266 WiFi Module [part_number=ESP8266]
  Slave_Arduino = Arduino Nano (Rev3.0) (ICSP)
  R1 = Resistor [tolerance=±5% resistance=220 package=THT]
  R2 = Resistor [tolerance=±5% resistance=220 package=THT]
  R3 = Resistor [tolerance=±5% resistance=220 package=THT]
  R4 = Resistor [tolerance=±5% resistance=220 package=THT]
  Led1_-_Wifi = LED - 5mm [color="Orange (620nm)" package="5 mm [THT]"]
  Led2_-_Clients = LED - 5mm [color="Yellow (595nm)" package="5 mm [THT]"]
  Led3_-_TX = LED - 5mm [color="Red (633nm)" package="5 mm [THT]"]
  Led4_-_RX = LED - 5mm [color="Green (570nm)" package="5 mm [THT]"]

nets:
  N1: part.RXD, Slave_Arduino.D1/TX
  GND: part.GND, Slave_Arduino.GND, R1.Pin_1, R2.Pin_1, R3.Pin_1, R4.Pin_1
  N2: part.TXD, Slave_Arduino.D0/RX
  N3: part.GPIO_16, Led1_-_Wifi.anode
  N4: part.GPIO_14, Led2_-_Clients.anode
  N5: part.GPIO_12, Led3_-_TX.anode
  N6: part.GPIO_13, Led4_-_RX.anode
  N7: R1.Pin_0, Led1_-_Wifi.cathode
  N8: R2.Pin_0, Led2_-_Clients.cathode
  N9: R3.Pin_0, Led3_-_TX.cathode
  N10: R4.Pin_0, Led4_-_RX.cathode
